# Fritzing sketch synerduino STM micr3-S1(2022) (saved by Fritzing 0.9.3b)
circuit board: 5.78556cm x 20cm
circuit board: 13.8cm x 6.5cm
circuit board: 5.78556cm x 20cm
breadboards: 1

parts:
  J1 = rounded female pin header, 20 pins [form="♀ (female rounded)"]
  J2 = rounded female pin header, 20 pins [form="♀ (female rounded)"]
  IMU2 = InvenSense MPU6050
  U1 = Voltage Regulator - 5V [package="TO220 [THT]"]
  S7 = male pin header, 3 pins [form="♂ (male)"]
  U2 = Voltage Regulator - 5V [package="TO220 [THT]"]
  D12 = Rectifier Diode [part_number=1N4001 package="300 mil [THT]"]
  -_+ = screw terminal, 2 pins
  -_+_2 = screw terminal, 2 pins
  -_+_3 = screw terminal, 2 pins
  -_+_4 = screw terminal, 2 pins
  -_+_5 = screw terminal, 2 pins
  S6 = male pin header, 3 pins [form="♂ (male)"]
  S5 = male pin header, 3 pins [form="♂ (male)"]
  S4 = male pin header, 3 pins [form="♂ (male)"]
  S3 = male pin header, 3 pins [form="♂ (male)"]
  S2 = male pin header, 3 pins [form="♂ (male)"]
  S1 = male pin header, 3 pins [form="♂ (male)"]
  UART1 = male pin header, 6 pins [form="♂ (male)"]
  IMU1 = InvenSense MPU6050
  UART2 = male pin header, 6 pins [form="♂ (male)"]
  Synerduino_STMF411 = Arduino Uno (Rev3)
  R1_51K = Resistor [tolerance=±5% resistance=51k package=THT]
  R2_10K = Resistor [tolerance=±5% resistance=10k package=THT]
  P10 = Pad [width=2.2000000000000002 height=2 connect=center]
  P11 = Pad [width=2.2000000000000002 height=2 connect=center]
  P12 = Pad [width=2.2000000000000002 height=2 connect=center]
  P9 = Pad [width=2.2000000000000002 height=2 connect=center]
  P8 = Pad [width=2.2000000000000002 height=2 connect=center]
  P7 = Pad [width=2.2000000000000002 height=2 connect=center]
  J3 = male pin header, 3 pins [form="♂ (male)"]
  UARTS = male pin header, 6 pins [form="♂ (male)"]
  3V = male pin header, 3 pins [form="♂ (male)"]
  P1 = Pad [width=2.2000000000000002 height=2 connect=center]
  P2 = Pad [width=2.2000000000000002 height=2 connect=center]
  P3 = Pad [width=2.2000000000000002 height=2 connect=center]
  P4 = Pad [width=2.2000000000000002 height=2 connect=center]
  R3_10K = Resistor [tolerance=±5% resistance=10k package=THT]
  R4_5k = Resistor [tolerance=±5% resistance=5k package=THT]
  P5 = Pad [width=2.2000000000000002 height=2 connect=center]
  P6 = Pad [width=2.2000000000000002 height=2 connect=center]
  J8 = male pin header, 8 pins [form="♂ (male)"]  # not connected
  J4 = male pin header, 8 pins [form="♂ (male)"]  # not connected
  J9 = male pin header, 8 pins [form="♂ (male)"]  # not connected
  J6 = male pin header, 8 pins [form="♂ (male)"]  # not connected
  J5 = male pin header, 8 pins [form="♂ (male)"]  # not connected
  J10 = male pin header, 10 pins [form="♂ (male)"]  # not connected
  C1 = Electrolytic Capacitor [capacitance=470µF voltage=35V package="100 mil [THT, electrolytic]"]
  C2 = Electrolytic Capacitor [capacitance=470µF voltage=35V package="100 mil [THT, electrolytic]"]
  R6_1K = Resistor [tolerance=±5% resistance=1k package=THT]
  R5_2K = Resistor [tolerance=±5% resistance=2k package=THT]
  J7 = male pin header, 3 pins [form="♂ (male)"]
  Q2 = NPN-Transistor [package="TO92 [THT]"]
  RC2 = male pin header, 3 pins [form="♂ (male)"]
  RC1 = male pin header, 3 pins [form="♂ (male)"]

nets:
  N1: J1.pin1, P9.pad
  GND: J1.pin2, J2.pin19, IMU2.GND, U1.GND, S7.pin3, U2.GND, -_+.pin2, -_+_2.pin2, -_+_3.pin2, -_+_4.pin2, -_+_5.pin2, S6.pin3, S5.pin3, S4.pin3, S3.pin3, S2.pin3, S1.pin3, UART1.pin2, IMU1.GND, UART2.pin2, Synerduino_STMF411.GND, R2_10K.Pin_1, J3.pin3, UARTS.pin2, C1.-, C2.-, R5_2K.Pin_1, J7.pin3, Q2.E, RC2.pin3, RC1.pin3
  N2: J1.pin4, S3.pin1, Synerduino_STMF411.A2
  N3: J1.pin6, P11.pad
  N4: J1.pin7, S7.pin1
  N5: J1.pin8, Synerduino_STMF411.D7
  N6: J1.pin9, Synerduino_STMF411.D6_PWM
  N7: J1.pin10, Synerduino_STMF411.D5_PWM
  N8: J1.pin11, Synerduino_STMF411.D4
  N9: J1.pin12, UART2.pin3, P5.pad, RC1.pin1
  N10: J1.pin13, UART2.pin4
  N11: J1.pin15, S5.pin1
  N12: J1.pin16, Synerduino_STMF411.RESET
  N13: J1.pin18, Synerduino_STMF411.D3_PWM
  N14: J1.pin19, Synerduino_STMF411.D2
  N15: J2.pin1, Synerduino_STMF411.D11_PWM/MOSI
  N16: J2.pin2, Synerduino_STMF411.D10_PWM/SS
  N17: J2.pin3, Synerduino_STMF411.D9_PWM
  N18: J2.pin4, Synerduino_STMF411.D8
  N19: J2.pin5, S1.pin1, Synerduino_STMF411.A0
  N20: J2.pin6, UART1.pin4
  N21: J2.pin7, UART1.pin3
  N22: J2.pin10, S4.pin1
  N23: J2.pin11, S2.pin1, Synerduino_STMF411.A1
  N24: J2.pin12, S6.pin1, Synerduino_STMF411.A3
  N25: J2.pin14, UARTS.pin4, P4.pad
  N26: J2.pin15, UARTS.pin3, P2.pad
  N27: J2.pin16, IMU2.SCL, UART1.pin5, IMU1.SCL, UART2.pin5, Synerduino_STMF411.A5/SCL, UARTS.pin5
  N28: J2.pin17, IMU2.SDA, UART1.pin6, IMU1.SDA, UART2.pin6, Synerduino_STMF411.A4/SDA, UARTS.pin6
  N29: J2.pin18, U2.output_voltage, UART1.pin1, UART2.pin1, UARTS.pin1, R3_10K.Pin_0, RC2.pin2, RC1.pin2
  VCC: J2.pin20, IMU2.VCC, IMU1.VCC, Synerduino_STMF411.3V3, 3V.pin1, 3V.pin2, 3V.pin3
  N30: U1.input_voltage, U2.input_voltage, D12.cathode
  N31: U1.output_voltage, P7.pad
  N32: S7.pin2, S6.pin2, S5.pin2, S4.pin2, S3.pin2, S2.pin2, S1.pin2, Synerduino_STMF411.VIN, P8.pad, J3.pin2, J7.pin2
  N33: D12.anode, -_+.pin1, -_+_2.pin1, -_+_3.pin1, -_+_4.pin1, -_+_5.pin1, R1_51K.Pin_1, C1.+, C2.+
  N34: Synerduino_STMF411.D12/MISO, R6_1K.Pin_1, J7.pin1
  N35: Synerduino_STMF411.D0/RX, P1.pad
  N36: Synerduino_STMF411.D1/TX, P3.pad
  N37: R1_51K.Pin_0, R2_10K.Pin_0, P10.pad
  N38: P12.pad, J3.pin1, R6_1K.Pin_0, R5_2K.Pin_0
  N39: R3_10K.Pin_1, P6.pad, Q2.C
  N40: R4_5k.Pin_0, RC2.pin1
  N41: R4_5k.Pin_1, Q2.B

notes:
  Tx Rx
  Rx Tx
  Soft Serial
  GPS UART1
  ~ + -
  Telemetey
  SBUS UART2
  5V
  RX
  TX
  SCL
  SDA
  +
  -
  ~
  REG
  BEC
  Vbat
  ADC
  MOSI
  MISO
  SCK
  CS
  ADC In
  - + ~
  SCL SDA
  BEEP
  LED
  TXSS
  RXSS
  S1
  S2
  S3
  S4
  2s-4s
  FLASH SD
  DIN
  DOUT
  MAX7456 OSD
  www.synerflight.com
  GND
  RC2 Inv
  2N2222A
  E B C
  Fold Regulator--->
  Front-->
  3V
  Gnd
  <-- USB Side
  6  7  8  9  10 11 12 13 14 15
  TX1
  RX1
  TX2
  RX2
  TX3
  RX3
  V0.1
  ADC 3v
  ADC 5v
